# Fritzing sketch Switch Network Arduino Shield (saved by Fritzing 0.8.7b)
circuit board: 6.9215cm x 5.33756cm
breadboards: 1

parts:
  Triggers = female pin header, 3 pins [form="♀ (female)"]
  J1 = female pin header, 4 pins [form="♀ (female)"]
  J2 = female pin header, 4 pins [form="♀ (female)"]
  Switching = LED - 5mm [color="Red (633nm)" package="5 mm [THT]"]
  R1 = Resistor [tolerance=±5% resistance=220 package=THT]
  UNO = Arduino Uno (Rev3)

nets:
  N1: Triggers.pin1, Switching.cathode, UNO.GND
  N2: Triggers.pin2, UNO.D2
  N3: Triggers.pin3, UNO.D3_PWM
  N4: J1.pin1, UNO.D4
  N5: J1.pin2, UNO.D5_PWM
  N6: J1.pin3, UNO.D6_PWM
  N7: J1.pin4, UNO.D7
  N8: J2.pin1, UNO.D9_PWM
  N9: J2.pin2, UNO.D10_PWM/SS
  N10: J2.pin3, UNO.D11_PWM/MOSI
  N11: J2.pin4, UNO.D12/MISO
  N12: Switching.anode, R1.Pin_1
  N13: R1.Pin_0, UNO.D13/SCK

notes:
  GND
  Inj Sw
  Stim
  DIN+
  DIN-
  SCLK
  SYNC
  RST
  VDD
  VSS
